// Logisim project MU0_Processor.circ as structural Verilog: 1 circuit, main circuit main
module main (
  input  in_1,
  input  in_2,
  input  in_3,
  input  in_4,
  input  in_5,
  input  in_6,
  input  up0down1,
  output a0,
  output out_9,
  output out_10,
  output a1,
  output out_12,
  output a2,
  output a3
);

  wire ADD, adder_2_cout, adder_2_out, adder_3_cout, adder_3_out, adder_4_cout, adder_4_out, adder_5_out,
       and_1_out, and_2_out, and_3_out, and_4_out, and_5_out, and_6_out, and_7_out, CLK2_out, clk_out,
       clock_1_out, clock_2_out, comparator_1_eq, comparator_1_gt, d_ff_1_q, d_ff_2_qn, d_ff_3_qn, d_ff_4_qn,
       decoder_1_out7, decoder_1_out8, decoder_1_out9, decoder_1_out10, decoder_1_out11, decoder_1_out12,
       decoder_1_out13, decoder_1_out14, decoder_1_out15, JGE, JMP, JNE, LDA, multiplexer_2_out,
       multiplexer_4_out, multiplexer_5_out, multiplexer_7_out, multiplexer_9_out, not_1_out, not_2_out,
       not_3_out, not_4_out, not_5_out, not_7_out, or_1_out, or_2_out, or_3_out, or_4_out, reset_out,
       RST_out, STO, STP, SUB;
  wire [3:0] ACC_q, ACC_q_2, ACC_q_3, ACC_q_4, bit_extender_1_out, multiplexer_8_out, multiplexer_8_out_2,
       multiplexer_8_out_3, PC_q, PC_q_2, PC_q_3;
  wire [11:0] adder_1_out, multiplexer_6_out;
  wire [15:0] adder_6_out, IR_q, multiplexer_10_out, multiplexer_11_out, not_6_out, RAMRAM_dout;

  Clock clock_1 (.out(clock_1_out));
  Clock clock_2 (.out(clock_2_out));
  Button RST (.out(RST_out));
  Clock CLK2 (.out(CLK2_out));
  not not_1 (not_1_out, in_2);
  Multiplexer multiplexer_1 (.in0(out_10), .in1(in_5), .out(out_10), .sel(clock_1_out));
  Multiplexer multiplexer_2 (.in0(multiplexer_2_out), .in1(in_6), .out(multiplexer_2_out), .sel(not_2_out));
  not not_2 (not_2_out, clock_2_out);
  not not_3 (not_3_out, d_ff_1_q);
  Multiplexer multiplexer_3 (.in0(out_12), .in1(multiplexer_2_out), .out(out_12), .sel(clock_2_out));
  Adder #(.width(12)) adder_1 (
    .a({PC_q_3, PC_q_2, PC_q}), .b({12{1'b0}}), .out(adder_1_out), .cin(1'b1));  // open: cout
  D_Flip_Flop d_ff_1 (.D(not_3_out), .clk(CLK2_out), .Q(d_ff_1_q), .reset(RST_out));  // open: Qn, preset
  // Transmission_Gate transmission_1: pin names not known; wires that end beside it: in_1, in_2, not_1_out, out_9
  // Transmission_Gate transmission_2: pin names not known; wires that end beside it: in_4, not_1_out, in_2, out_9
  or or_1 (or_1_out, and_7_out, JMP, and_6_out);
  or or_2 (or_2_out, and_6_out, JMP, and_7_out, d_ff_1_q);
  Multiplexer multiplexer_4 (.in0(adder_3_cout), .in1(and_3_out), .out(multiplexer_4_out), .sel(up0down1));
  Multiplexer multiplexer_5 (.in0(adder_4_cout), .in1(and_2_out), .out(multiplexer_5_out), .sel(up0down1));
  Hex_Digit_Display hex_digit_display_1 (.value(PC_q_3));  // open: dp
  Hex_Digit_Display hex_digit_display_2 (.value(PC_q_2));  // open: dp
  Multiplexer #(.width(12)) multiplexer_6 (
    .in0(adder_1_out), .in1(IR_q[11:0]), .out(multiplexer_6_out), .sel(or_1_out));
  and and_1 (and_1_out, or_2_out, STP);
  not not_4 (not_4_out, d_ff_1_q);
  Multiplexer multiplexer_7 (.in0(adder_2_cout), .in1(d_ff_2_qn), .out(multiplexer_7_out), .sel(up0down1));
  and and_2 (and_2_out, and_3_out, d_ff_4_qn);
  Hex_Digit_Display hex_digit_display_3 (.value(PC_q));  // open: dp
  Register #(.width(12)) PC (
    .D(multiplexer_6_out), .en(and_1_out), .clk(CLK2_out), .Q({PC_q_3, PC_q_2, PC_q}), .clr(RST_out));
  Adder #(.width(1)) adder_2 (.a(a0), .b(in_3), .out(adder_2_out), .cout(adder_2_cout));  // open: cin
  Adder #(.width(1)) adder_3 (.a(a1), .b(multiplexer_7_out), .out(adder_3_out), .cout(adder_3_cout));  // open: cin
  and and_3 (and_3_out, d_ff_2_qn, d_ff_3_qn);
  Adder #(.width(1)) adder_4 (.a(a2), .b(multiplexer_4_out), .out(adder_4_out), .cout(adder_4_cout));  // open: cin
  Adder #(.width(1)) adder_5 (.a(a3), .b(multiplexer_5_out), .out(adder_5_out));  // open: cin, cout
  Clock clk (.out(clk_out));
  D_Flip_Flop d_ff_2 (.D(adder_2_out), .clk(clk_out), .Q(a0), .Qn(d_ff_2_qn), .reset(reset_out));  // open: preset
  D_Flip_Flop d_ff_3 (.D(adder_3_out), .clk(clk_out), .Q(a1), .Qn(d_ff_3_qn), .reset(reset_out));  // open: preset
  D_Flip_Flop d_ff_4 (.D(adder_4_out), .clk(clk_out), .Q(a2), .Qn(d_ff_4_qn), .reset(reset_out));  // open: preset
  D_Flip_Flop d_ff_5 (.D(adder_5_out), .clk(clk_out), .Q(a3), .reset(reset_out));  // open: Qn, preset
  Button reset (.out(reset_out));
  Hex_Digit_Display hex_digit_display_4 (.value(multiplexer_8_out_3));  // open: dp
  Multiplexer #(.width(12)) multiplexer_8 (
    .in0({PC_q_3, PC_q_2, PC_q}), .in1(IR_q[11:0]),
    .out({multiplexer_8_out_3, multiplexer_8_out_2, multiplexer_8_out}), .sel(d_ff_1_q));
  not not_5 (not_5_out, CLK2_out);
  Multiplexer multiplexer_9 (.in0(1'b0), .in1(1'b1), .out(multiplexer_9_out), .sel(SUB));
  Hex_Digit_Display hex_digit_display_5 (.value(multiplexer_8_out_2));  // open: dp
  Hex_Digit_Display hex_digit_display_6 (.value(multiplexer_8_out));  // open: dp
  assign not_6_out = ~RAMRAM_dout;  // NOT_Gate not_6, 16 bits wide
  and and_4 (and_4_out, STO, not_5_out, d_ff_1_q);
  // Probe on multiplexer_10_out
  Multiplexer #(.width(16)) multiplexer_10 (
    .in0({ACC_q_4, ACC_q_3, ACC_q_2, ACC_q}), .in1({16{1'b0}}), .out(multiplexer_10_out), .sel(LDA));
  Multiplexer #(.width(16)) multiplexer_11 (
    .in0(RAMRAM_dout), .in1(not_6_out), .out(multiplexer_11_out), .sel(multiplexer_9_out));
  // Probe on multiplexer_11_out
  RAM #(.addrWidth(12), .asyncread("true"), .dataWidth(16)) RAMRAM (
    .addr({multiplexer_8_out_3, multiplexer_8_out_2, multiplexer_8_out}), .we(and_4_out), .oe(1'b1),
    .clk(CLK2_out), .din({ACC_q_4, ACC_q_3, ACC_q_2, ACC_q}), .dout(RAMRAM_dout));
  Adder #(.width(16)) adder_6 (
    .a(multiplexer_10_out), .b(multiplexer_11_out), .out(adder_6_out), .cin(multiplexer_9_out));  // open: cout
  or or_3 (or_3_out, LDA, SUB, ADD);
  // Probe on adder_6_out
  and and_5 (and_5_out, or_3_out, d_ff_1_q);
  // Probe on RAMRAM_dout
  Register #(.width(16)) ACC (
    .D(adder_6_out), .en(and_5_out), .clk(CLK2_out), .Q({ACC_q_4, ACC_q_3, ACC_q_2, ACC_q}), .clr(RST_out));
  Comparator #(.width(16)) comparator_1 (
    .a({ACC_q_4, ACC_q_3, ACC_q_2, ACC_q}), .b({16{1'b0}}), .gt(comparator_1_gt), .eq(comparator_1_eq));  // open: lt
  Hex_Digit_Display hex_digit_display_7 (.value(ACC_q_4));  // open: dp
  Hex_Digit_Display hex_digit_display_8 (.value(ACC_q_3));  // open: dp
  or or_4 (or_4_out, comparator_1_gt, comparator_1_eq);
  Hex_Digit_Display hex_digit_display_9 (.value(ACC_q_2));  // open: dp
  Hex_Digit_Display hex_digit_display_10 (.value(ACC_q));  // open: dp
  Register #(.width(16)) IR (.D(RAMRAM_dout), .en(not_4_out), .clk(CLK2_out), .Q(IR_q), .clr(RST_out));
  not not_7 (not_7_out, comparator_1_eq);
  and and_6 (and_6_out, or_4_out, JGE);
  // Probe on IR_q[11:0]
  assign bit_extender_1_out = {{3{1'b0}}, d_ff_1_q};  // Bit_Extender bit_extender_1
  and and_7 (and_7_out, not_7_out, JNE);
  Hex_Digit_Display hex_digit_display_11 (.value(IR_q[15:12]));  // open: dp
  Hex_Digit_Display hex_digit_display_12 (.value(bit_extender_1_out));  // open: dp
  Decoder #(.select(4)) decoder_1 (
    .out0(LDA), .out1(STO), .out2(ADD), .out3(SUB), .out4(JMP), .out5(JGE), .out6(JNE),
    .out7(decoder_1_out7), .out8(decoder_1_out8), .out9(decoder_1_out9), .out10(decoder_1_out10),
    .out11(decoder_1_out11), .out12(decoder_1_out12), .out13(decoder_1_out13), .out14(decoder_1_out14),
    .out15(decoder_1_out15), .sel(IR_q[15:12]));  // open: en
  nor nor_1 (STP, decoder_1_out7, decoder_1_out8, decoder_1_out9, decoder_1_out10, decoder_1_out11, decoder_1_out12, decoder_1_out13, decoder_1_out14, decoder_1_out15);
endmodule
